# Fritzing sketch ArduXWeatherStation Receiver (saved by Fritzing 0.9.1b)

parts:
  U1 = RF-LINK_RX [package=rf-link_rx]
  Componente1 = Arduino Mega 2560 (Rev3)
  Componente2 = 3.5in TFT 480x320 Touch + MicroSD  # not connected

nets:
  GND: U1.GND, Componente1.GND
  N1: U1.Data, Componente1.D44
  VCC: U1.VCC, Componente1.5V

notes:
  PROJECT
  Ardu Xively Weather Station Receiver
  HW Ver. 1.0
  - Freeduino Mega 2560.
  - RF Link receiver 433Mhz 5V with external antenna of 17.3cm, soldering of ANT
  - TFT Touch screen 3.2".
  Note:
  - Use only screens 3.2-inch TFT Touch (no 3.5 inch).
  - Connect arduino Mega 2560 as written in the product datasheet.
  - If the PIN Data 44, the 5V and GND of the XD-RF-5V 433Mhz receiver were committed by the connections of the TFT, for PIN Data use another digital, the 5V and GND use those near the PIN 3V, change the sketch with the new PIN Data.

custom parts:
  RF-LINK_RX: RF Link receivers- WRL-8947, 8948, 8949, 8950
  3.5in TFT 480x320 Touch + MicroSD: This TFT display is big (3.5" diagonal), bright (6 white-LED backlight) and colorful! 480x320 pixels with individual RGB pixel control. This display also has a resistive touchscreen attached to it already, so you can detect finger presses anywhere on the screen. There is a controller built into the display with RAM buffering, so that almost no work is done by the microcontroller. The display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

// code stored in the sketch: RF_RX_Lamp Code.ino
// receiver.pde
//
// Simple example of how to use VirtualWire to receive messages
// Implements a simplex (one-way) receiver with an Rx-B1 module
//
// See VirtualWire.h for detailed API docs
// Author: Mike McCauley (mikem@airspayce.com)
// Copyright (C) 2008 Mike McCauley
// $Id: receiver.pde,v 1.3 2009/03/30 00:07:24 mikem Exp $

#include <VirtualWire.h>

const int led_pin = 13;
const int transmit_pin = 11;
const int receive_pin = 12;
const int transmit_en_pin = 3;
int time_out = 5000;

void setup()
{
    delay(1000);
    Serial.begin(9600);	// Debugging only
    Serial.println("setup");

    // Initialise the IO and ISR
    vw_set_tx_pin(transmit_pin);
    vw_set_rx_pin(receive_pin);
    vw_set_ptt_pin(transmit_en_pin);
    vw_set_ptt_inverted(true); // Required for DR3100
    vw_setup(2000);	 // Bits per sec

    vw_rx_start();       // Start the receiver PLL running

    pinMode(led_pin, OUTPUT);
}

void loop()
{
    uint8_t buf[VW_MAX_MESSAGE_LEN];
    uint8_t buflen = VW_MAX_MESSAGE_LEN;

if (vw_wait_rx_max(time_out))
    {
    if (vw_get_message(buf, &buflen)) // Non-blocking
    	{
	int i;

        digitalWrite(led_pin, HIGH); // Flash a light to show received good message
	// Message with a good checksum received, dump it.
	Serial.print("Got: ");
	
	for (i = 0; i < buflen; i++)
	{
	    Serial.print(buf[i], HEX);
	    Serial.print(' ');
	}
	Serial.println();
		digitalWrite(led_pin, HIGH);
	
    	}
    }
    else
    digitalWrite(led_pin, LOW);
}
