# Fritzing sketch ArduXWeatherStation (saved by Fritzing 0.9.1b)
breadboards: 1

parts:
  RHT1 = Humidity and Temperature Sensor RHT03
  R1 = Resistor [tolerance=±5% resistance=4.7k package=THT]
  Componente1 = Barometric Pressure Sensor - BMP085 Breakout
  Componente2 = Logic Level Converter
  Componente3 = Real Time Clock Module - DS1307 RTC Breakout Board
  C1 = Ceramic Capacitor [capacitance=100nF package="100 mil [THT, multilayer]"]
  R2 = Resistor [tolerance=±1% resistance=2.4k package=THT]
  R3 = Resistor [tolerance=±1% resistance=2.4k package=THT]
  R4 = Resistor [tolerance=±1% resistance=2.4k package=THT]
  R5 = Resistor [tolerance=±1% resistance=2.4k package=THT]
  R6 = Resistor [tolerance=±1% resistance=2.4k package=THT]
  R7 = Resistor [tolerance=±1% resistance=2.4k package=THT]
  Componente4 = Arduino Ethernet Shield (Rev3)  # not connected
  Componente5 = Arduino Mega 2560 (Rev3)
  U1 = mystery part, 3 pins [chip_label=UVM-30A]
  Componente6 = BH1750
  U3 = CHJ-FST1000M [package=CHJ-FST1000M]

nets:
  5V: RHT1.Vcc, R1.Pin_1, Componente3.5V, C1.0, R4.Pin_1, R5.Pin_1, R6.Pin_1, R7.Pin_1, Componente5.5V, U1.pin3, U3.+5V
  N1: RHT1.Data-signal, R1.Pin_0, Componente5.D2_PWM
  GND: RHT1.GND_2, Componente1.GND, Componente2.GND, Componente3.GND, C1.1, Componente5.GND, U1.pin1, Componente6.GND, U3.GND
  VCC: Componente1.VCC, Componente2.LV, R2.Pin_0, R3.Pin_0, Componente5.3V3
  N2: Componente1.SCL, Componente2.TX_LV, R3.Pin_1
  N3: Componente1.SDA, Componente2.TX2_LV, R2.Pin_1
  N4: Componente2.TX_HV, Componente3.SCL, R5.Pin_0, R7.Pin_0, Componente5.D21/SCL, Componente6.SCL
  N5: Componente2.TX2_HV, Componente3.SDA, R4.Pin_0, R6.Pin_0, Componente5.D20/SDA, Componente6.SDA
  N6: Componente5.A8, U1.pin2
  N7: Componente5.D44, U3.DATA

notes:
  PROJECT
  Ardu Xively Weather Station
  HW Ver. 1.1
  - Freeduino Mega 2560.
  - Ethernet Shield
  - Sensor BMP085 3.3V I2C
  - Logic Level Converter
  - RTC 5V I2C
  - Sensor DHT22 5V
  - GY-30 BH1750FVI intensity digital sensor light module I2C with build-in LLC 5V
  - UVM-30A UV Light sensor
  - RF FS1000A transmitter 433Mhz 5V with external antenna of 17.3cm, soldering of ANT
  - Resistor 4.7K e
  - Resistors 2.4K for pull up
  - Ceramic capacitor 100nF
  - Cables dupont
  - (option) mini router HX701 set as "CLIENT MODE" to connect Arduino ethernet shield, turns the ethernet connection in WiFi.

custom parts:
  BH1750: Light Sensor
  CHJ-FST1000M: RF LINK
